// Logisim project 16bit_Adder.circ as structural Verilog: 1 circuit, main circuit main
module main (
  input  in_1,
  input  [7:0] _1L,
  input  [7:0] _1H,
  input  [7:0] _2L,
  input  [7:0] _2H,
  input  [7:0] in_6,
  output CARRY,
  output [7:0] ZL,
  output [7:0] ZH,
  output [7:0] ZL_2,
  output CARRY_2
);

  Adder adder_1 (.a(_1L), .b(_2L), .out(ZL), .cin(in_1), .cout(CARRY));
  Adder adder_2 (.a(_1H), .b(_2H), .out(ZH), .cin(CARRY), .cout(CARRY_2));
  assign ZL_2 = ZH & in_6;  // AND_Gate and_1, 8 bits wide
endmodule
