// Logisim project CPU_ALU.circ as structural Verilog: 2 circuits, main circuit ALU
module ALU (
  input  [2:0] OP,
  input  [7:0] A,
  input  [7:0] B,
  output [7:0] R,
  output Z,
  output C,
  output N
);

  wire alu1bit_1_cout, alu1bit_2_cout, alu1bit_3_cout, alu1bit_4_cout, alu1bit_5_cout, alu1bit_6_cout,
       alu1bit_7_cout, and_1_out;

  and and_1 (and_1_out, OP[2], ~OP[1], OP[0]);  // AND_Gate
  ALU1Bit alu1bit_1 (.X(A[0]), .Y(B[0]), .Cin(and_1_out), .Sub(and_1_out), .OP(OP), .Cout(alu1bit_1_cout), .Z(R[0]));
  ALU1Bit alu1bit_2 (
    .X(A[1]), .Y(B[1]), .Cin(alu1bit_1_cout), .Sub(and_1_out), .OP(OP), .Cout(alu1bit_2_cout), .Z(R[1]));
  ALU1Bit alu1bit_3 (
    .X(A[2]), .Y(B[2]), .Cin(alu1bit_2_cout), .Sub(and_1_out), .OP(OP), .Cout(alu1bit_3_cout), .Z(R[2]));
  ALU1Bit alu1bit_4 (
    .X(A[3]), .Y(B[3]), .Cin(alu1bit_3_cout), .Sub(and_1_out), .OP(OP), .Cout(alu1bit_4_cout), .Z(R[3]));
  ALU1Bit alu1bit_5 (
    .X(A[4]), .Y(B[4]), .Cin(alu1bit_4_cout), .Sub(and_1_out), .OP(OP), .Cout(alu1bit_5_cout), .Z(R[4]));
  ALU1Bit alu1bit_6 (
    .X(A[5]), .Y(B[5]), .Cin(alu1bit_5_cout), .Sub(and_1_out), .OP(OP), .Cout(alu1bit_6_cout), .Z(R[5]));
  ALU1Bit alu1bit_7 (
    .X(A[6]), .Y(B[6]), .Cin(alu1bit_6_cout), .Sub(and_1_out), .OP(OP), .Cout(alu1bit_7_cout), .Z(R[6]));
  ALU1Bit alu1bit_8 (.X(A[7]), .Y(B[7]), .Cin(alu1bit_7_cout), .Sub(and_1_out), .OP(OP), .Cout(C), .Z(N));
  nor nor_1 (Z, R[0], R[1], R[2], R[3], R[4], R[5], R[6], N);

  assign R[7] = N;

  // Notes on the sheet:
  //   ALU 8BIT
endmodule

module ALU1Bit (
  input  Cin,
  input  Sub,
  input  [2:0] OP,
  input  X,
  input  Y,
  output Z,
  output Cout
);

  wire adder_1_out, and_1_out, nor_1_out, or_1_out, xor_1_out, xor_2_out;

  xor xor_1 (xor_1_out, Y, Sub);
  and and_1 (and_1_out, X, Y);
  or or_1 (or_1_out, X, Y);
  nor nor_1 (nor_1_out, X, Y);
  xor xor_2 (xor_2_out, X, Y);
  Adder #(.width(1)) adder_1 (.a(X), .b(xor_1_out), .out(adder_1_out), .cin(Cin), .cout(Cout));
  Multiplexer #(.select(3), .enable("false")) multiplexer_1 (
    .in0(and_1_out), .in1(or_1_out), .in2(nor_1_out), .in3(xor_2_out), .in4(adder_1_out), .in5(adder_1_out),
    .out(Z), .sel(OP));  // open: in6, in7

  // Notes on the sheet:
  //   ALU 1BIT
endmodule
