// Logisim project CPU_Test_001.circ as structural Verilog: 2 circuits, main circuit main
module main (
  input  in_1,
  output [7:0] IN_BUS,
  output [7:0] OUT_BUS,
  output [7:0] out_4
);

  wire clock_1_out, nor_1_out, not_1_out;
  wire [7:0] AD_q, AX_q, BX_q, controlled_buffer_1_out, controlled_buffer_9_out, CX_q, DR_q, DX_q, IP_q, OP_q;
  wire [23:0] rom_1_data;

  Clock clock_1 (.out(clock_1_out));
  not not_1 (not_1_out, rom_1_data[11]);
  assign controlled_buffer_1_out = not_1_out ? AD_q : 8'bz;  // Controlled_Buffer controlled_buffer_1
  assign controlled_buffer_1_out = rom_1_data[11] ? OP_q : 8'bz;  // Controlled_Buffer controlled_buffer_2
  assign rom_1_data[11] = in_1 ? 1'b0 : 1'bz;  // Controlled_Buffer controlled_buffer_3
  ROM #(.dataWidth(32)) rom_1 (.addr(controlled_buffer_1_out), .data({out_4, rom_1_data}), .sel(1'b1));
  Register_part AD (.D(out_4), .Q(AD_q), .clk(clock_1_out));  // open: en, clr
  Register AX (.D(IN_BUS), .W(rom_1_data[0]), .C(clock_1_out), .R(rom_1_data[1]), .Q(AX_q));
  Register BX (.D(IN_BUS), .W(rom_1_data[2]), .C(clock_1_out), .R(rom_1_data[3]), .Q(BX_q));
  Register CX (.D(IN_BUS), .W(rom_1_data[4]), .C(clock_1_out), .R(rom_1_data[5]), .Q(CX_q));
  Register DX (.D(IN_BUS), .W(rom_1_data[6]), .C(clock_1_out), .R(rom_1_data[7]), .Q(DX_q));
  Register IP (.D(IN_BUS), .W(rom_1_data[8]), .C(clock_1_out), .R(rom_1_data[9]), .Q(IP_q));
  Register OP (.D(IN_BUS), .W(rom_1_data[10]), .C(clock_1_out), .R(rom_1_data[11]), .Q(OP_q));
  Register DR (.D(IN_BUS), .W(rom_1_data[12]), .C(clock_1_out), .R(rom_1_data[13]), .Q(DR_q));
  assign OUT_BUS = rom_1_data[1] ? AX_q : 8'bz;  // Controlled_Buffer controlled_buffer_4
  assign OUT_BUS = rom_1_data[3] ? BX_q : 8'bz;  // Controlled_Buffer controlled_buffer_5
  assign OUT_BUS = rom_1_data[5] ? CX_q : 8'bz;  // Controlled_Buffer controlled_buffer_6
  assign OUT_BUS = rom_1_data[7] ? DX_q : 8'bz;  // Controlled_Buffer controlled_buffer_7
  assign OUT_BUS = rom_1_data[9] ? IP_q : 8'bz;  // Controlled_Buffer controlled_buffer_8
  assign controlled_buffer_9_out = rom_1_data[13] ? DR_q : 8'bz;  // Controlled_Buffer controlled_buffer_9
  assign controlled_buffer_9_out = nor_1_out ? {8{1'b0}} : 8'bz;  // Controlled_Buffer controlled_buffer_10
  nor nor_1 (nor_1_out, rom_1_data[13], rom_1_data[14]);
  assign controlled_buffer_9_out = rom_1_data[14] ? 8'h1 : 8'bz;  // Controlled_Buffer controlled_buffer_11
  Adder adder_1 (.a(OUT_BUS), .b(controlled_buffer_9_out), .out(IN_BUS));  // open: cin, cout
  RAM ram_1 ();  // open: addr, data, sel, clk, ld, clr

  // Notes on the sheet:
  //   OPCODES
  //   contents of rom_1 (hex, n*v repeats v):
  //   1000000 2004003 6
  //   ALU
endmodule

module Register (
  input  [7:0] D,
  input  W,
  input  C,
  input  R,
  output [7:0] Q
);

  wire buffer_2_out, buffer_3_out, buffer_4_out;
  wire [7:0] and_1_out, buffer_1_out, register_1_q;

  assign buffer_1_out = D;  // Buffer buffer_1, 8 bits wide
  buf buffer_2 (buffer_2_out, W);
  buf buffer_3 (buffer_3_out, C);
  buf buffer_4 (buffer_4_out, R);
  Register_part register_1 (.D(buffer_1_out), .en(buffer_2_out), .Q(register_1_q), .clk(buffer_3_out));  // open: clr
  and and_1 (and_1_out[0], buffer_4_out, register_1_q[0]);
  and and_2 (and_1_out[1], buffer_4_out, register_1_q[1]);
  and and_3 (and_1_out[2], buffer_4_out, register_1_q[2]);
  and and_4 (and_1_out[3], buffer_4_out, register_1_q[3]);
  and and_5 (and_1_out[4], buffer_4_out, register_1_q[4]);
  and and_6 (and_1_out[5], buffer_4_out, register_1_q[5]);
  and and_7 (and_1_out[6], buffer_4_out, register_1_q[6]);
  and and_8 (and_1_out[7], buffer_4_out, register_1_q[7]);
  assign Q = and_1_out;  // Buffer buffer_5, 8 bits wide
endmodule
