// Logisim project CPU_Test_002.circ as structural Verilog: 1 circuit, main circuit CPU
module CPU (
  output [7:0] out_1,
  output [2:0] OPCODE,
  output [7:0] out_3,
  output [7:0] out_4,
  output [7:0] S
);

  wire and_1_out, clock_1_out, not_1_out, or_1_out, or_2_out, RESET_out;
  wire [7:0] alu_1_r, AR_H_q, AR_L_q, AX_q, BX_q, controlled_buffer_1_out, controlled_buffer_3_out,
       controlled_buffer_4_out, controlled_buffer_5_out, controlled_buffer_6_out, controlled_buffer_9_out,
       controlled_buffer_10_out, controlled_buffer_11_out, controlled_buffer_12_out,
       controlled_buffer_13_out, controlled_buffer_14_out, controlled_buffer_16_out, CX_q, DR_q,
       led8x8_1_out_column_l_r, led8x8_1_out_row_l, led8x8_1_out_row_r, OP_prime_q, OP_q, PCH_q, PCL_q,
       ram_1_data, rom_1_data, rom_2_data, rom_3_data, STP_q;
  wire [15:0] adder_1_out, PC_q;

  assign controlled_buffer_1_out = rom_3_data[7] ? {8{1'b0}} : 8'bz;  // Controlled_Buffer controlled_buffer_1
  assign controlled_buffer_1_out = rom_3_data[6] ? out_1 : 8'bz;  // Controlled_Buffer controlled_buffer_2
  or or_1 (or_1_out, rom_3_data[7], rom_3_data[6]);
  assign controlled_buffer_3_out = rom_2_data[4] ? controlled_buffer_16_out : 8'bz;  // Controlled_Buffer controlled_buffer_3
  assign controlled_buffer_4_out = rom_2_data[5] ? controlled_buffer_16_out : 8'bz;  // Controlled_Buffer controlled_buffer_4
  Register OP_prime (.D(controlled_buffer_1_out), .en(or_1_out), .Q(OP_prime_q), .clk(clock_1_out), .clr(RESET_out));
  assign controlled_buffer_5_out = rom_3_data[7] ? OP_prime_q : 8'bz;  // Controlled_Buffer controlled_buffer_5
  not not_1 (not_1_out, rom_3_data[7]);
  Register AR_L (.D(controlled_buffer_3_out), .Q(AR_L_q), .clk(clock_1_out), .clr(RESET_out));  // open: en
  Register AR_H (.D(controlled_buffer_4_out), .Q(AR_H_q), .clk(clock_1_out), .clr(RESET_out));  // open: en
  Counter OP (
    .load(rom_3_data[7]), .D(controlled_buffer_5_out), .count(not_1_out), .Q(OP_q), .clk(clock_1_out),
    .clr(RESET_out));  // open: carry
  or or_2 (or_2_out, rom_3_data[0], rom_3_data[1]);
  ROM rom_1 (.addr(OP_q), .data(rom_1_data));  // open: sel
  ROM rom_2 (.addr(OP_q), .data(rom_2_data));  // open: sel
  ROM rom_3 (.addr(OP_q), .data({rom_3_data[7:5], OPCODE, rom_3_data[1:0]}));  // open: sel
  RAM #(.addrWidth(13)) ram_1 (
    .addr({AR_H_q[4:0], AR_L_q}), .data(ram_1_data), .sel(or_2_out), .clk(clock_1_out), .ld(rom_3_data[1]),
    .clr(RESET_out));
  assign controlled_buffer_6_out = rom_2_data[6] ? controlled_buffer_16_out : 8'bz;  // Controlled_Buffer controlled_buffer_6
  assign ram_1_data = rom_3_data[0] ? DR_q : 8'bz;  // Controlled_Buffer controlled_buffer_7
  assign controlled_buffer_6_out = rom_3_data[1] ? ram_1_data : 8'bz;  // Controlled_Buffer controlled_buffer_8
  Button RESET (.out(RESET_out));
  assign controlled_buffer_9_out = rom_2_data[7] ? DR_q : 8'bz;  // Controlled_Buffer controlled_buffer_9
  Register DR (.D(controlled_buffer_6_out), .Q(DR_q), .clk(clock_1_out), .clr(RESET_out));  // open: en
  Clock clock_1 (.out(clock_1_out));
  assign controlled_buffer_10_out = rom_1_data[0] ? out_1 : 8'bz;  // Controlled_Buffer controlled_buffer_10
  assign controlled_buffer_11_out = rom_1_data[2] ? out_1 : 8'bz;  // Controlled_Buffer controlled_buffer_11
  assign controlled_buffer_12_out = rom_1_data[4] ? out_1 : 8'bz;  // Controlled_Buffer controlled_buffer_12
  assign controlled_buffer_13_out = rom_1_data[6] ? out_1 : 8'bz;  // Controlled_Buffer controlled_buffer_13
  assign controlled_buffer_14_out = rom_2_data[0] ? out_1 : 8'bz;  // Controlled_Buffer controlled_buffer_14
  assign controlled_buffer_14_out = rom_2_data[2] ? out_1 : 8'bz;  // Controlled_Buffer controlled_buffer_15
  Register AX (.D(controlled_buffer_10_out), .Q(AX_q), .clk(clock_1_out), .clr(RESET_out));  // open: en
  assign controlled_buffer_16_out = rom_1_data[1] ? AX_q : 8'bz;  // Controlled_Buffer controlled_buffer_16
  assign controlled_buffer_16_out = rom_1_data[3] ? BX_q : 8'bz;  // Controlled_Buffer controlled_buffer_17
  Register BX (.D(controlled_buffer_11_out), .Q(BX_q), .clk(clock_1_out), .clr(RESET_out));  // open: en
  assign controlled_buffer_16_out = rom_1_data[5] ? CX_q : 8'bz;  // Controlled_Buffer controlled_buffer_18
  Register CX (.D(controlled_buffer_12_out), .Q(CX_q), .clk(clock_1_out), .clr(RESET_out));  // open: en
  Register #(.trigger("falling")) PCL (
    .D(controlled_buffer_13_out), .Q(PCL_q), .clk(clock_1_out), .clr(RESET_out));  // open: en
  assign controlled_buffer_16_out = rom_1_data[7] ? PCL_q : 8'bz;  // Controlled_Buffer controlled_buffer_19
  Register #(.trigger("falling")) PCH (
    .D(controlled_buffer_14_out), .Q(PCH_q), .clk(clock_1_out), .clr(RESET_out));  // open: en
  assign controlled_buffer_16_out = rom_2_data[1] ? PCH_q : 8'bz;  // Controlled_Buffer controlled_buffer_20
  assign controlled_buffer_16_out = rom_2_data[3] ? STP_q : 8'bz;  // Controlled_Buffer controlled_buffer_21
  Register STP (.D(controlled_buffer_14_out), .Q(STP_q), .clk(clock_1_out), .clr(RESET_out));  // open: en
  Pull_Resistor pull_resistor_1 (.node(out_3));
  assign out_3 = controlled_buffer_16_out;  // Buffer buffer_1, 8 bits wide
  assign controlled_buffer_9_out = rom_3_data[5] ? 8'h1 : 8'bz;  // Controlled_Buffer controlled_buffer_22
  assign out_4 = controlled_buffer_9_out;  // Buffer buffer_2, 8 bits wide
  Pull_Resistor pull_resistor_2 (.node(out_4));
  Register #(.width(16)) PC (.D({PCH_q, PCL_q}), .en(clock_1_out), .Q(PC_q), .clk(clock_1_out), .clr(RESET_out));
  LED8x8 led8x8_1 (
    .CLOCK(clock_1_out), .OUT_ROW_L(led8x8_1_out_row_l), .OUT_ROW_R(led8x8_1_out_row_r),
    .OUT_COLUMN_L_R(led8x8_1_out_column_l_r));  // open: INTERRUPT, LED_BLANK, IN_L, IN_R
  Adder #(.width(16)) adder_1 (.a(PC_q), .b(16'h1), .out(adder_1_out));  // open: cin, cout
  and and_1 (and_1_out, rom_1_data[7], rom_3_data[5]);
  ALU alu_1 (.A(out_3), .B(out_4), .OP(OPCODE), .R(alu_1_r), .Z(S[5]), .C(S[6]), .N(S[7]));
  assign controlled_buffer_13_out = and_1_out ? adder_1_out[7:0] : 8'bz;  // Controlled_Buffer controlled_buffer_23
  assign controlled_buffer_14_out = and_1_out ? adder_1_out[15:8] : 8'bz;  // Controlled_Buffer controlled_buffer_24
  assign out_1 = alu_1_r;  // Buffer buffer_3, 8 bits wide
  // DotMatrix #(.inputtype("select"), .matrixcols(8), .matrixrows(8)) dotmatrix_1: pin names not known; wires that end beside it: led8x8_1_out_row_l
  // DotMatrix #(.inputtype("select"), .matrixcols(8), .matrixrows(8)) dotmatrix_2: pin names not known; wires that end beside it: led8x8_1_out_row_r, led8x8_1_out_column_l_r

  // Notes on the sheet:
  //   CPU
  //   contents of rom_1 (hex, n*v repeats v):
  //   80 0 0 0 c0 80 0 0 c0 0 1 0 4 0 12 0 4 c0 10 8 20 0 1
  //   contents of rom_2 (hex, n*v repeats v):
  //   10 22 0 80 0 10 22 0 0 0 80 0 80 0 80 0 80 0 80 10 20 0 80
  //   contents of rom_3 (hex, n*v repeats v):
  //   0 0 2 40 30 0 0 2 30 80 0 80 0 80 10 80 0 30 0 0 0 2 0 80
  //   Z C N
endmodule
