// Logisim project CPU_Test_003.circ as structural Verilog: 2 circuits, main circuit CPU
module CPU (
  input  in_1,
  input  [7:0] in_2,
  input  [7:0] in_3,
  output [7:0] out_4,
  output [7:0] out_5,
  output [7:0] out_6,
  output [2:0] OPCODE,
  output [7:0] out_8,
  output [7:0] out_9,
  output [7:0] S,
  output [7:0] out_11
);

  wire and_1_out, and_2_out, clock_1_out, led8x8_1_led_blank, nor_1_out, not_1_out, not_2_out, or_1_out,
       or_2_out, RESET_out, subtractor_1_bout, subtractor_2_bout;
  wire [7:0] alu_1_r, AX_q, BX_q, controlled_buffer_1_out, controlled_buffer_3_out, controlled_buffer_4_out,
       controlled_buffer_5_out, controlled_buffer_6_out, controlled_buffer_9_out, controlled_buffer_10_out,
       controlled_buffer_11_out, controlled_buffer_12_out, controlled_buffer_13_out,
       controlled_buffer_14_out, controlled_buffer_16_out, CX_q, DR_q, led8x8_1_out_column_l_r,
       led8x8_1_out_row_l, led8x8_1_out_row_r, OP_prime_q, OP_q, rom_1_data, STP_q;
  wire [7:5] AR_H_q;
  wire [9:0] subtractor_1_out;
  wire [10:0] subtractor_2_out;
  wire [12:0] AR_L_q;
  wire [12:10] subtractor_1_out_2;
  wire [12:11] subtractor_2_out_2;
  wire [15:0] adder_1_out, PC_q;
  wire [23:0] rom_2_data;

  assign controlled_buffer_1_out = rom_2_data[7] ? {8{1'b0}} : 8'bz;  // Controlled_Buffer controlled_buffer_1
  assign controlled_buffer_1_out = rom_2_data[6] ? out_6 : 8'bz;  // Controlled_Buffer controlled_buffer_2
  or or_1 (or_1_out, rom_2_data[7], rom_2_data[6]);
  assign controlled_buffer_3_out = rom_2_data[12] ? controlled_buffer_16_out : 8'bz;  // Controlled_Buffer controlled_buffer_3
  assign controlled_buffer_4_out = rom_2_data[13] ? controlled_buffer_16_out : 8'bz;  // Controlled_Buffer controlled_buffer_4
  ROM #(.addrWidth(10)) rom_1 (.addr(subtractor_1_out), .data(rom_1_data), .sel(nor_1_out));
  assign controlled_buffer_5_out = rom_2_data[7] ? OP_prime_q : 8'bz;  // Controlled_Buffer controlled_buffer_5
  Register OP_prime (.D(controlled_buffer_1_out), .en(or_1_out), .Q(OP_prime_q), .clk(clock_1_out), .clr(RESET_out));
  not not_1 (not_1_out, rom_2_data[7]);
  Register AR_L (.D(controlled_buffer_3_out), .Q(AR_L_q[7:0]), .clk(clock_1_out), .clr(RESET_out));  // open: en
  Register AR_H (
    .D(controlled_buffer_4_out), .Q({AR_H_q, AR_L_q[12:8]}), .clk(clock_1_out), .clr(RESET_out));  // open: en
  Subtractor #(.width(13)) subtractor_1 (
    .a(AR_L_q), .b(13'h800), .out({subtractor_1_out_2, subtractor_1_out}), .bout(subtractor_1_bout));  // open: bin
  Counter OP (
    .load(rom_2_data[7]), .D(controlled_buffer_5_out), .count(not_1_out), .Q(OP_q), .clk(clock_1_out),
    .clr(RESET_out));  // open: carry
  and and_1 (and_1_out, subtractor_1_bout, or_2_out);
  or or_2 (or_2_out, rom_2_data[1], rom_2_data[0]);
  ROM #(.dataWidth(24)) rom_2 (.addr(OP_q), .data({rom_2_data[23:5], OPCODE, rom_2_data[1:0]}));  // open: sel
  RAM #(.addrWidth(13)) ram_1 (
    .addr(AR_L_q), .data(rom_1_data), .sel(and_1_out), .clk(clock_1_out), .ld(rom_2_data[1]), .clr(RESET_out));
  Subtractor #(.width(13)) subtractor_2 (
    .a(AR_L_q), .b(13'h1c00), .out({subtractor_2_out_2, subtractor_2_out}), .bout(subtractor_2_bout));  // open: bin
  assign controlled_buffer_6_out = rom_2_data[14] ? controlled_buffer_16_out : 8'bz;  // Controlled_Buffer controlled_buffer_6
  assign rom_1_data = rom_2_data[0] ? DR_q : 8'bz;  // Controlled_Buffer controlled_buffer_7
  assign controlled_buffer_6_out = rom_2_data[1] ? rom_1_data : 8'bz;  // Controlled_Buffer controlled_buffer_8
  not not_2 (not_2_out, subtractor_2_bout);
  Button RESET (.out(RESET_out));
  assign controlled_buffer_9_out = rom_2_data[15] ? DR_q : 8'bz;  // Controlled_Buffer controlled_buffer_9
  Register DR (.D(controlled_buffer_6_out), .Q(DR_q), .clk(clock_1_out), .clr(RESET_out));  // open: en
  LED led_1 (.in(subtractor_1_bout));
  LED led_2 (.in(not_2_out));
  LED led_3 (.in(nor_1_out));
  nor nor_1 (nor_1_out, not_2_out, subtractor_1_bout);
  Clock clock_1 (.out(clock_1_out));
  assign controlled_buffer_10_out = rom_2_data[16] ? out_6 : 8'bz;  // Controlled_Buffer controlled_buffer_10
  assign controlled_buffer_11_out = rom_2_data[18] ? out_6 : 8'bz;  // Controlled_Buffer controlled_buffer_11
  assign controlled_buffer_12_out = rom_2_data[20] ? out_6 : 8'bz;  // Controlled_Buffer controlled_buffer_12
  assign controlled_buffer_13_out = rom_2_data[22] ? out_6 : 8'bz;  // Controlled_Buffer controlled_buffer_13
  assign controlled_buffer_14_out = rom_2_data[8] ? out_6 : 8'bz;  // Controlled_Buffer controlled_buffer_14
  assign controlled_buffer_14_out = rom_2_data[10] ? out_6 : 8'bz;  // Controlled_Buffer controlled_buffer_15
  Register AX (.D(controlled_buffer_10_out), .Q(AX_q), .clk(clock_1_out), .clr(RESET_out));  // open: en
  assign controlled_buffer_16_out = rom_2_data[17] ? AX_q : 8'bz;  // Controlled_Buffer controlled_buffer_16
  Register BX (.D(controlled_buffer_11_out), .Q(BX_q), .clk(clock_1_out), .clr(RESET_out));  // open: en
  assign controlled_buffer_16_out = rom_2_data[19] ? BX_q : 8'bz;  // Controlled_Buffer controlled_buffer_17
  assign controlled_buffer_16_out = rom_2_data[21] ? CX_q : 8'bz;  // Controlled_Buffer controlled_buffer_18
  Register CX (.D(controlled_buffer_12_out), .Q(CX_q), .clk(clock_1_out), .clr(RESET_out));  // open: en
  REGISTER PCL (.D(controlled_buffer_13_out), .RST(RESET_out), .RST_VAL({8{1'b0}}), .Q(out_4), .CLK(clock_1_out));
  REGISTER PCH (.D(controlled_buffer_14_out), .RST(RESET_out), .RST_VAL(8'h1c), .Q(out_5), .CLK(clock_1_out));
  Register STP (.D(controlled_buffer_14_out), .Q(STP_q), .clk(clock_1_out), .clr(RESET_out));  // open: en
  assign controlled_buffer_16_out = rom_2_data[23] ? out_4 : 8'bz;  // Controlled_Buffer controlled_buffer_19
  assign controlled_buffer_16_out = rom_2_data[9] ? out_5 : 8'bz;  // Controlled_Buffer controlled_buffer_20
  assign controlled_buffer_16_out = rom_2_data[11] ? STP_q : 8'bz;  // Controlled_Buffer controlled_buffer_21
  Pull_Resistor pull_resistor_1 (.node(out_8));
  assign out_8 = controlled_buffer_16_out;  // Buffer buffer_1, 8 bits wide
  assign controlled_buffer_9_out = rom_2_data[5] ? 8'h1 : 8'bz;  // Controlled_Buffer controlled_buffer_22
  assign out_9 = controlled_buffer_9_out;  // Buffer buffer_2, 8 bits wide
  Pull_Resistor pull_resistor_2 (.node(out_9));
  LED led_4 (.in(led8x8_1_led_blank));
  Register #(.width(16)) PC (.D({out_5, out_4}), .en(clock_1_out), .Q(PC_q), .clk(clock_1_out), .clr(RESET_out));
  and and_2 (and_2_out, rom_2_data[23], rom_2_data[5]);
  ROM #(.addrWidth(11)) rom_3 (.addr(subtractor_2_out), .data(rom_1_data), .sel(not_2_out));
  LED8x8 led8x8_1 (
    .CLOCK(clock_1_out), .INTERRUPT(in_1), .LED_BLANK(led8x8_1_led_blank), .IN_L(in_3), .IN_R(in_2),
    .OUT_ROW_L(led8x8_1_out_row_l), .OUT_ROW_R(led8x8_1_out_row_r), .OUT_COLUMN_L_R(led8x8_1_out_column_l_r));
  Adder #(.width(16)) adder_1 (.a(PC_q), .b(16'h1), .out(adder_1_out));  // open: cin, cout
  ALU alu_1 (.A(out_8), .B(out_9), .OP(OPCODE), .R(alu_1_r), .Z(S[5]), .C(S[6]), .N(S[7]));
  assign controlled_buffer_13_out = and_2_out ? adder_1_out[7:0] : 8'bz;  // Controlled_Buffer controlled_buffer_23
  assign controlled_buffer_14_out = and_2_out ? adder_1_out[15:8] : 8'bz;  // Controlled_Buffer controlled_buffer_24
  assign out_6 = alu_1_r;  // Buffer buffer_3, 8 bits wide
  // DotMatrix #(.inputtype("select"), .matrixcols(8), .matrixrows(8)) dotmatrix_1: pin names not known; wires that end beside it: led8x8_1_out_row_l
  // DotMatrix #(.inputtype("select"), .matrixcols(8), .matrixrows(8)) dotmatrix_2: pin names not known; wires that end beside it: led8x8_1_out_row_r, led8x8_1_out_column_l_r

  // Notes on the sheet:
  //   ROM
  //   contents of rom_1 (hex, n*v repeats v):
  //   a 22 c 44 1d 1f fc
  //   OP
  //   RAM
  //   contents of rom_2 (hex, n*v repeats v):
  //   801000 2200 2 8040 c00030 801000 2200 2 c00030 80 18000 80 48000 80 48000 801000 2200 2 108000
  //   201000 82020 2 18000 80 48000 82020 2 18000 80 48000 801000 2200 2 108000 600000 80100 80
  //   RAM ACCESS
  //   KERNEL ACCESS
  //   ROM ACCESS
  //   contents of rom_3 (hex, n*v repeats v):
  //   1d 8 1018*0 1d 1f fc
  //   ALU
  //   Z C N
endmodule

module REGISTER (
  input  CLK,
  input  [7:0] D,
  input  RST,
  input  [7:0] RST_VAL,
  output [7:0] Q
);

  wire [7:0] controlled_buffer_1_out, not_1_out;

  assign controlled_buffer_1_out = RST ? RST_VAL : 8'bz;  // Controlled_Buffer controlled_buffer_1
  assign not_1_out = ~controlled_buffer_1_out;  // NOT_Gate not_1, 8 bits wide
  D_Flip_Flop d_ff_1 (
    .clk(CLK), .D(D[0]), .Q(Q[0]), .preset(controlled_buffer_1_out[0]), .reset(not_1_out[0]));  // open: Qn, en
  D_Flip_Flop d_ff_2 (
    .clk(CLK), .D(D[1]), .Q(Q[1]), .preset(controlled_buffer_1_out[1]), .reset(not_1_out[1]));  // open: Qn, en
  D_Flip_Flop d_ff_3 (
    .clk(CLK), .D(D[2]), .Q(Q[2]), .preset(controlled_buffer_1_out[2]), .reset(not_1_out[2]));  // open: Qn, en
  D_Flip_Flop d_ff_4 (
    .clk(CLK), .D(D[3]), .Q(Q[3]), .preset(controlled_buffer_1_out[3]), .reset(not_1_out[3]));  // open: Qn, en
  D_Flip_Flop d_ff_5 (
    .clk(CLK), .D(D[4]), .Q(Q[4]), .preset(controlled_buffer_1_out[4]), .reset(not_1_out[4]));  // open: Qn, en
  D_Flip_Flop d_ff_6 (
    .clk(CLK), .D(D[5]), .Q(Q[5]), .preset(controlled_buffer_1_out[5]), .reset(not_1_out[5]));  // open: Qn, en
  D_Flip_Flop d_ff_7 (
    .clk(CLK), .D(D[6]), .Q(Q[6]), .preset(controlled_buffer_1_out[6]), .reset(not_1_out[6]));  // open: Qn, en
  D_Flip_Flop d_ff_8 (
    .clk(CLK), .D(D[7]), .Q(Q[7]), .preset(controlled_buffer_1_out[7]), .reset(not_1_out[7]));  // open: Qn, en

  // Notes on the sheet:
  //   CLK: pull=down
endmodule
