// Logisim project LED8x8.circ as structural Verilog: 1 circuit, main circuit LED8x8
// LED
module LED8x8 (
  input  CLOCK,
  input  INTERRUPT,
  input  [7:0] IN_L,
  input  [7:0] IN_R,
  output [7:0] OUT_ROW_L,
  output [7:0] OUT_ROW_R,
  output [7:0] OUT_COLUMN_L_R,
  output LED_BLANK
);

  wire and_1_out, and_2_out, not_1_out, or_1_out, READ___WRITE_q, READ___WRITE_qn, register_1_q;
  wire [2:0] counter_1_q;
  wire [7:0] ram_1_data, ram_2_data;

  or or_1 (or_1_out, and_1_out, and_2_out);
  J_K_Flip_Flop READ___WRITE (
    .J(or_1_out), .clk(CLOCK), .K(or_1_out), .Q(READ___WRITE_q), .Qn(READ___WRITE_qn));  // open: preset, en, reset
  and and_1 (and_1_out, READ___WRITE_q, LED_BLANK);
  and and_2 (and_2_out, LED_BLANK, register_1_q);
  Register #(.width(1)) register_1 (.D(INTERRUPT), .Q(register_1_q), .clk(CLOCK));  // open: en, clr
  not not_1 (not_1_out, LED_BLANK);
  Counter #(.width(4), .max('hf)) counter_1 (
    .load(LED_BLANK), .D(4'b0000), .count(not_1_out), .Q({LED_BLANK, counter_1_q}), .clk(CLOCK));  // open: carry, clr
  RAM #(.addrWidth(3)) ram_1 (
    .addr(counter_1_q), .data(ram_1_data), .clk(CLOCK), .ld(READ___WRITE_qn));  // open: sel, clr
  assign ram_1_data = READ___WRITE_q ? IN_L : 8'bz;  // Controlled_Buffer controlled_buffer_1
  RAM #(.addrWidth(3)) ram_2 (
    .addr(counter_1_q), .data(ram_2_data), .clk(CLOCK), .ld(READ___WRITE_qn));  // open: sel, clr
  assign ram_2_data = READ___WRITE_q ? IN_R : 8'bz;  // Controlled_Buffer controlled_buffer_2
  assign OUT_ROW_L = READ___WRITE_qn ? ram_1_data : 8'bz;  // Controlled_Buffer controlled_buffer_3
  assign OUT_ROW_R = READ___WRITE_qn ? ram_2_data : 8'bz;  // Controlled_Buffer controlled_buffer_4
  Shift_Register shift_register_1 (
    .shift(1'b1), .in(LED_BLANK), .clk(CLOCK), .q0(OUT_COLUMN_L_R[7]), .q1(OUT_COLUMN_L_R[6]),
    .q2(OUT_COLUMN_L_R[5]), .q3(OUT_COLUMN_L_R[4]), .q4(OUT_COLUMN_L_R[3]), .q5(OUT_COLUMN_L_R[2]),
    .q6(OUT_COLUMN_L_R[1]), .q7(OUT_COLUMN_L_R[0]));  // open: out, load, clr, d0, d1, d2, d3, d4, d5, d6, d7

  // Notes on the sheet:
  //   8x16 DOT MATRIX CONTROLLER
  //   LEFT
  //   RIGHT
endmodule
