// Logisim project PC.circ as structural Verilog: 1 circuit, main circuit main
module main (
  input  ENABLE_IN_H,
  input  ENABLE_IN_L,
  input  ENABLE_OUT_H,
  input  ENABLE_OUT_L,
  input  [7:0] IN_H,
  input  [7:0] IN_L,
  input  RST,
  input  CLK,
  input  plus_1,
  output [7:0] OUT_H,
  output [7:0] OUT_L
);

  wire [7:0] controlled_buffer_1_out, controlled_buffer_2_out, controlled_buffer_3_out,
       controlled_buffer_4_out, register_1_q, register_2_q;
  wire [15:0] adder_1_out;

  assign controlled_buffer_1_out = ENABLE_IN_L ? IN_L : 8'bz;  // Controlled_Buffer controlled_buffer_1
  assign controlled_buffer_2_out = ENABLE_IN_H ? IN_H : 8'bz;  // Controlled_Buffer controlled_buffer_2
  Register register_1 (.D(controlled_buffer_2_out), .Q(register_1_q), .clk(CLK), .clr(RST));  // open: en
  assign controlled_buffer_3_out = plus_1 ? register_1_q : 8'bz;  // Controlled_Buffer controlled_buffer_3
  assign controlled_buffer_4_out = plus_1 ? register_2_q : 8'bz;  // Controlled_Buffer controlled_buffer_4
  Register register_2 (.D(controlled_buffer_1_out), .Q(register_2_q), .clk(CLK), .clr(RST));  // open: en
  assign controlled_buffer_1_out = plus_1 ? adder_1_out[7:0] : 8'bz;  // Controlled_Buffer controlled_buffer_5
  Adder #(.width(16)) adder_1 (
    .a({controlled_buffer_3_out, controlled_buffer_4_out}), .b(16'h1), .out(adder_1_out));  // open: cin, cout
  assign controlled_buffer_2_out = plus_1 ? adder_1_out[15:8] : 8'bz;  // Controlled_Buffer controlled_buffer_6
  assign OUT_H = ENABLE_OUT_H ? register_1_q : 8'bz;  // Controlled_Buffer controlled_buffer_7
  assign OUT_L = ENABLE_OUT_L ? register_2_q : 8'bz;  // Controlled_Buffer controlled_buffer_8
endmodule
