// Logisim project REGISTER.circ as structural Verilog: 1 circuit, main circuit main
module main (
  input  CLK,
  input  [7:0] D,
  input  RST,
  input  [7:0] RST_VAL,
  output [7:0] Q
);

  wire [7:0] controlled_buffer_1_out, not_1_out;

  assign controlled_buffer_1_out = RST ? RST_VAL : 8'bz;  // Controlled_Buffer controlled_buffer_1
  assign not_1_out = ~controlled_buffer_1_out;  // NOT_Gate not_1, 8 bits wide
  D_Flip_Flop d_ff_1 (
    .clk(CLK), .D(D[0]), .Q(Q[0]), .preset(controlled_buffer_1_out[0]), .reset(not_1_out[0]));  // open: Qn, en
  D_Flip_Flop d_ff_2 (
    .clk(CLK), .D(D[1]), .Q(Q[1]), .preset(controlled_buffer_1_out[1]), .reset(not_1_out[1]));  // open: Qn, en
  D_Flip_Flop d_ff_3 (
    .clk(CLK), .D(D[2]), .Q(Q[2]), .preset(controlled_buffer_1_out[2]), .reset(not_1_out[2]));  // open: Qn, en
  D_Flip_Flop d_ff_4 (
    .clk(CLK), .D(D[3]), .Q(Q[3]), .preset(controlled_buffer_1_out[3]), .reset(not_1_out[3]));  // open: Qn, en
  D_Flip_Flop d_ff_5 (
    .clk(CLK), .D(D[4]), .Q(Q[4]), .preset(controlled_buffer_1_out[4]), .reset(not_1_out[4]));  // open: Qn, en
  D_Flip_Flop d_ff_6 (
    .clk(CLK), .D(D[5]), .Q(Q[5]), .preset(controlled_buffer_1_out[5]), .reset(not_1_out[5]));  // open: Qn, en
  D_Flip_Flop d_ff_7 (
    .clk(CLK), .D(D[6]), .Q(Q[6]), .preset(controlled_buffer_1_out[6]), .reset(not_1_out[6]));  // open: Qn, en
  D_Flip_Flop d_ff_8 (
    .clk(CLK), .D(D[7]), .Q(Q[7]), .preset(controlled_buffer_1_out[7]), .reset(not_1_out[7]));  // open: Qn, en

  // Notes on the sheet:
  //   CLK: pull=down
endmodule
