// Logisim project CPU.circ as structural Verilog: 8 circuits, main circuit MAIN
module MAIN (
);

  wire CLK_out, RESET_out;
  wire [7:0] ALU_z, AX_probe_out, BX_probe_out, CU_probe_op, RAM_out, RAM_probe_dr, SP_probe_out;
  wire [15:0] PC_probe_out, RAM_probe_address;
  wire [23:0] CU_out_6;

  // Probe on CU_probe_op
  // Probe on CU_out_6
  // Probe on RAM_probe_address
  // Probe on RAM_probe_dr
  CU CU (
    .IN(RAM_out), .CLOCK(CLK_out), .RESET(RESET_out), .PROBE_OP(CU_probe_op), .SET_OP(CU_out_6[15]),
    .out_6(CU_out_6));
  RAM RAM (
    .RESET(RESET_out), .CLK(CLK_out), .ENABLE_H(CU_out_6[23]), .ENABLE_L(CU_out_6[22]), .R(CU_out_6[21]),
    .W(CU_out_6[20]), .DR_I(CU_out_6[19]), .DR_O(CU_out_6[18]), .PROBE_ADDRESS(RAM_probe_address),
    .PROBE_DR(RAM_probe_dr), .IN(RAM_out), .OUT(RAM_out));
  ALU ALU (.X(AX_probe_out), .Y(RAM_out), .OP(CU_out_6[13:10]), .Z(ALU_z));  // open: C_I, C_O
  Button RESET (.out(RESET_out));
  PC PC (
    .IN_L(RAM_out), .IN_H(RAM_out), .ENABLE_IN_L(CU_out_6[4]), .ENABLE_IN_H(CU_out_6[5]),
    .ENABLE_OUT_L(CU_out_6[6]), .ENABLE_OUT_H(CU_out_6[7]), .plus_1(CU_out_6[14]), .CLK(CLK_out),
    .RESET(RESET_out), .OUT_L(RAM_out), .OUT_H(RAM_out), .PROBE_OUT(PC_probe_out));
  // Probe on RAM_out
  Clock CLK (.out(CLK_out));
  REGISTER AX (
    .IN(RAM_out), .ENABLE_IN(CU_out_6[0]), .ENABLE_OUT(CU_out_6[1]), .OUT(RAM_out), .CLK(CLK_out),
    .RESET(RESET_out), .PROBE_OUT(AX_probe_out));
  REGISTER BX (
    .IN(RAM_out), .ENABLE_IN(CU_out_6[2]), .ENABLE_OUT(CU_out_6[3]), .OUT(RAM_out), .CLK(CLK_out),
    .RESET(RESET_out), .PROBE_OUT(BX_probe_out));
  REGISTER SP (
    .IN(RAM_out), .ENABLE_IN(CU_out_6[9]), .ENABLE_OUT(CU_out_6[8]), .OUT(RAM_out), .CLK(CLK_out),
    .RESET(RESET_out), .PROBE_OUT(SP_probe_out));
  // Probe on AX_probe_out
  // Probe on BX_probe_out
  // Probe on PC_probe_out
  // Probe on SP_probe_out
endmodule

module REGISTER (
  input  [7:0] IN,
  input  ENABLE_IN,
  input  ENABLE_OUT,
  input  CLK,
  input  RESET,
  output [7:0] OUT,
  output [7:0] PROBE_OUT
);

  wire [7:0] controlled_buffer_1_out;

  assign controlled_buffer_1_out = ENABLE_IN ? IN : 8'bz;  // Controlled_Buffer controlled_buffer_1
  Register register_1 (.D(controlled_buffer_1_out), .Q(PROBE_OUT), .clk(CLK), .clr(RESET));  // open: en
  assign OUT = ENABLE_OUT ? PROBE_OUT : 8'bz;  // Controlled_Buffer controlled_buffer_2
endmodule

module RAM (
  input  RESET,
  input  CLK,
  input  ENABLE_H,
  input  ENABLE_L,
  input  R,
  input  W,
  input  DR_I,
  input  DR_O,
  input  [7:0] IN,
  output [7:0] OUT,
  output [15:0] PROBE_ADDRESS,
  output [7:0] PROBE_DR
);

  wire or_1_out;
  wire [7:0] ram_1_data;

  REGISTER AR_L (
    .IN(IN), .ENABLE_IN(ENABLE_L), .ENABLE_OUT(1'b1), .OUT(PROBE_ADDRESS[7:0]), .CLK(CLK), .RESET(RESET));  // open: PROBE_OUT
  REGISTER AR_H (
    .IN(IN), .ENABLE_IN(ENABLE_H), .ENABLE_OUT(1'b1), .OUT(PROBE_ADDRESS[15:8]), .CLK(CLK), .RESET(RESET));  // open: PROBE_OUT
  // Probe on PROBE_ADDRESS
  or or_1 (or_1_out, W, R);
  RAM_part #(.addrWidth(16)) ram_1 (
    .addr(PROBE_ADDRESS), .data(ram_1_data), .sel(or_1_out), .clk(CLK), .ld(R), .clr(RESET));
  assign ram_1_data = W ? OUT : 8'bz;  // Controlled_Buffer controlled_buffer_1
  assign IN = R ? ram_1_data : 8'bz;  // Controlled_Buffer controlled_buffer_2
  REGISTER register_1 (
    .IN(IN), .ENABLE_IN(DR_I), .ENABLE_OUT(DR_O), .OUT(OUT), .CLK(CLK), .RESET(RESET), .PROBE_OUT(PROBE_DR));
endmodule

module PC (
  input  [7:0] IN_L,
  input  [7:0] IN_H,
  input  ENABLE_IN_L,
  input  ENABLE_IN_H,
  input  ENABLE_OUT_L,
  input  ENABLE_OUT_H,
  input  plus_1,
  input  CLK,
  input  RESET,
  output [7:0] OUT_L,
  output [7:0] OUT_H,
  output [15:0] PROBE_OUT
);

  wire [7:0] controlled_buffer_1_out, controlled_buffer_2_out, controlled_buffer_4_out,
       controlled_buffer_5_out;
  wire [15:0] adder_1_out;

  assign controlled_buffer_1_out = ENABLE_IN_L ? IN_L : 8'bz;  // Controlled_Buffer controlled_buffer_1
  assign controlled_buffer_2_out = ENABLE_IN_H ? IN_H : 8'bz;  // Controlled_Buffer controlled_buffer_2
  Register register_1 (.D(controlled_buffer_1_out), .Q(PROBE_OUT[7:0]), .clk(CLK), .clr(RESET));  // open: en
  assign OUT_H = ENABLE_OUT_H ? PROBE_OUT[15:8] : 8'bz;  // Controlled_Buffer controlled_buffer_3
  Register register_2 (.D(controlled_buffer_2_out), .Q(PROBE_OUT[15:8]), .clk(CLK), .clr(RESET));  // open: en
  assign controlled_buffer_4_out = plus_1 ? PROBE_OUT[7:0] : 8'bz;  // Controlled_Buffer controlled_buffer_4
  assign controlled_buffer_5_out = plus_1 ? PROBE_OUT[15:8] : 8'bz;  // Controlled_Buffer controlled_buffer_5
  assign OUT_L = ENABLE_OUT_L ? PROBE_OUT[7:0] : 8'bz;  // Controlled_Buffer controlled_buffer_6
  Adder #(.width(16)) adder_1 (
    .a({controlled_buffer_5_out, controlled_buffer_4_out}), .b(16'h1), .out(adder_1_out));  // open: cin, cout
  assign controlled_buffer_1_out = plus_1 ? adder_1_out[7:0] : 8'bz;  // Controlled_Buffer controlled_buffer_7
  assign controlled_buffer_2_out = plus_1 ? adder_1_out[15:8] : 8'bz;  // Controlled_Buffer controlled_buffer_8
endmodule

module CU (
  input  [7:0] IN,
  input  CLOCK,
  input  RESET,
  input  SET_OP,
  output [7:0] PROBE_OP,
  output [23:0] out_6
);

  wire comparator_1_eq, comparator_2_eq, not_1_out, not_2_out, not_3_out, or_1_out, or_2_out;
  wire [7:0] controlled_buffer_1_out, counter_1_q;
  wire [23:0] rom_1_data;

  not not_1 (not_1_out, CLOCK);
  Register OP (.D(controlled_buffer_1_out), .en(SET_OP), .Q(PROBE_OP), .clk(CLOCK), .clr(RESET));
  assign controlled_buffer_1_out = SET_OP ? IN : 8'bz;  // Controlled_Buffer controlled_buffer_1
  not not_2 (not_2_out, comparator_1_eq);
  Counter counter_1 (
    .load(comparator_1_eq), .D(PROBE_OP), .count(not_2_out), .Q(counter_1_q), .clk(not_1_out), .clr(or_1_out));  // open: carry
  or or_1 (or_1_out, RESET, comparator_2_eq);
  ROM #(.dataWidth(24)) rom_1 (.addr(counter_1_q), .data(rom_1_data), .sel(1'b1));
  Comparator #(.width(24)) comparator_1 (.a(rom_1_data), .b({24{1'b1}}), .eq(comparator_1_eq));  // open: gt, lt
  Comparator #(.width(24)) comparator_2 (.a(rom_1_data), .b({24{1'b0}}), .eq(comparator_2_eq));  // open: gt, lt
  Pull_Resistor pull_resistor_1 (.node(out_6));
  assign out_6 = not_3_out ? rom_1_data : 24'bz;  // Controlled_Buffer controlled_buffer_2
  not not_3 (not_3_out, or_2_out);
  or or_2 (or_2_out, comparator_1_eq, comparator_2_eq);

  // Notes on the sheet:
  //   CONTROL UNIT
  //   RESET COUNTER
  //   JUMP TO OP
  //   contents of rom_1 (hex, n*v repeats v):
  //   400040 800080 280000 46000 400040 800080 282000 ffffff 40001
endmodule

module ALU (
  input  [7:0] X,
  input  [7:0] Y,
  input  C_I,
  input  [3:0] OP,
  output C_O,
  output [7:0] Z
);

  wire and_2_out;
  wire [7:0] and_1_out, fulladder_8bit_1_z, or_1_out, shifter_1_out, shifter_2_out, shifter_3_out,
       shifter_4_out, shifter_5_out, xor_1_out;

  FULLADDER_8BIT fulladder_8bit_1 (.X(X), .Y(Y), .SUB(and_2_out), .C_IN(C_I), .Z(fulladder_8bit_1_z), .C_OUT(C_O));
  assign and_1_out = X & Y;  // AND_Gate and_1, 8 bits wide
  assign or_1_out = X | Y;  // OR_Gate or_1, 8 bits wide
  assign xor_1_out = X ^ Y;  // XOR_Gate xor_1, 8 bits wide
  Shifter shifter_1 (.in(X), .\dist (3'b001), .out(shifter_1_out));
  Shifter #(.shift("lr")) shifter_2 (.in(X), .\dist (3'b001), .out(shifter_2_out));
  Shifter #(.shift("ar")) shifter_3 (.in(X), .\dist (3'b001), .out(shifter_3_out));
  Shifter #(.shift("rl")) shifter_4 (.in(X), .\dist (3'b001), .out(shifter_4_out));
  Shifter #(.shift("rr")) shifter_5 (.in(X), .\dist (3'b001), .out(shifter_5_out));
  and and_2 (and_2_out, OP[0], ~OP[1], ~OP[2], ~OP[3]);  // AND_Gate
  Multiplexer #(.select(4), .width(8), .disabled(0), .enable("false")) multiplexer_1 (
    .in0(fulladder_8bit_1_z), .in1(fulladder_8bit_1_z), .in2(and_1_out), .in3(or_1_out), .in4(xor_1_out),
    .in5(shifter_1_out), .in6(shifter_2_out), .in7(shifter_3_out), .in8(shifter_4_out), .in9(shifter_5_out),
    .out(Z), .sel(OP));  // open: in10, in11, in12, in13, in14, in15
endmodule

module FULLADDER_1BIT (
  input  X,
  input  Y,
  input  C_IN,
  output C_OUT,
  output Z
);

  wire and_1_out, and_2_out, xor_1_out;

  and and_1 (and_1_out, X, Y);
  xor xor_1 (xor_1_out, X, Y);
  or or_1 (C_OUT, and_1_out, and_2_out);
  and and_2 (and_2_out, xor_1_out, C_IN);
  xor xor_2 (Z, xor_1_out, C_IN);
endmodule

// +/-
module FULLADDER_8BIT (
  input  [7:0] X,
  input  [7:0] Y,
  input  SUB,
  input  C_IN,
  output [7:0] Z,
  output C_OUT
);

  wire fulladder_1bit_1_c_out, fulladder_1bit_2_c_out, fulladder_1bit_3_c_out, fulladder_1bit_4_c_out,
       fulladder_1bit_5_c_out, fulladder_1bit_6_c_out, fulladder_1bit_7_c_out, or_1_out, xor_1_out,
       xor_2_out, xor_3_out, xor_4_out, xor_5_out, xor_6_out, xor_7_out, xor_8_out;

  or or_1 (or_1_out, SUB, C_IN);
  xor xor_1 (xor_1_out, SUB, Y[0]);
  xor xor_2 (xor_2_out, SUB, Y[1]);
  xor xor_3 (xor_3_out, SUB, Y[2]);
  xor xor_4 (xor_4_out, SUB, Y[3]);
  xor xor_5 (xor_5_out, SUB, Y[4]);
  xor xor_6 (xor_6_out, SUB, Y[5]);
  xor xor_7 (xor_7_out, SUB, Y[6]);
  xor xor_8 (xor_8_out, SUB, Y[7]);
  FULLADDER_1BIT fulladder_1bit_1 (.X(X[0]), .Y(xor_1_out), .C_IN(or_1_out), .C_OUT(fulladder_1bit_1_c_out), .Z(Z[0]));
  FULLADDER_1BIT fulladder_1bit_2 (
    .X(X[1]), .Y(xor_2_out), .C_IN(fulladder_1bit_1_c_out), .C_OUT(fulladder_1bit_2_c_out), .Z(Z[1]));
  FULLADDER_1BIT fulladder_1bit_3 (
    .X(X[2]), .Y(xor_3_out), .C_IN(fulladder_1bit_2_c_out), .C_OUT(fulladder_1bit_3_c_out), .Z(Z[2]));
  FULLADDER_1BIT fulladder_1bit_4 (
    .X(X[3]), .Y(xor_4_out), .C_IN(fulladder_1bit_3_c_out), .C_OUT(fulladder_1bit_4_c_out), .Z(Z[3]));
  FULLADDER_1BIT fulladder_1bit_5 (
    .X(X[4]), .Y(xor_5_out), .C_IN(fulladder_1bit_4_c_out), .C_OUT(fulladder_1bit_5_c_out), .Z(Z[4]));
  FULLADDER_1BIT fulladder_1bit_6 (
    .X(X[5]), .Y(xor_6_out), .C_IN(fulladder_1bit_5_c_out), .C_OUT(fulladder_1bit_6_c_out), .Z(Z[5]));
  FULLADDER_1BIT fulladder_1bit_7 (
    .X(X[6]), .Y(xor_7_out), .C_IN(fulladder_1bit_6_c_out), .C_OUT(fulladder_1bit_7_c_out), .Z(Z[6]));
  FULLADDER_1BIT fulladder_1bit_8 (.X(X[7]), .Y(xor_8_out), .C_IN(fulladder_1bit_7_c_out), .C_OUT(C_OUT), .Z(Z[7]));
endmodule
