// Logisim project CPU.circ as structural Verilog: 13 circuits, main circuit CPU
module CPU (
);

  wire A_out, alu_1_c_o, B_out, button_2_out, button_3_out, button_out, ccr_1_bi, ccr_1_c, ccr_1_n, ccr_1_z,
       clock_1_out, not_1_out, not_2_out, or_1_out, RESET_out, sp_1_error, V_out;
  wire [2:0] key_1_o;
  wire [3:0] controlled_buffer_1_out;
  wire [4:0] io_1_led_o, io_1_led_o_2, io_1_led_o_3, io_1_led_o_4, io_1_led_o_5;
  wire [7:0] alu_1_z, AX_probe_out, BX_probe_out, cu_1_probe_op, io_1_probe_dr, pc_1_o, sp_1_probe_out,
       Z_2_probe_out;
  wire [23:0] cu_1_o;

  DotMatrix #(.inputtype("row"), .matrixrows(5), .persist(150)) dotmatrix_1 (
    .row0(io_1_led_o_5), .row1(io_1_led_o_4), .row2(io_1_led_o_3), .row3(io_1_led_o_2), .row4(io_1_led_o));
  Button button (.out(button_out));
  Button button_2 (.out(button_2_out));
  // Probe on cu_1_probe_op
  CU cu_1 (.I(pc_1_o), .CLK(clock_1_out), .RST(RESET_out), .O(cu_1_o), .OP_I(cu_1_o[23]), .PROBE_OP(cu_1_probe_op));
  or or_1 (or_1_out, cu_1_o[22], ccr_1_bi);
  PC pc_1 (
    .O(pc_1_o), .I(io_1_probe_dr), .CLK(clock_1_out), .RST(RESET_out), .PC_I(or_1_out), .PC_O(cu_1_o[21]),
    .plus_1(cu_1_o[20]));
  IO io_1 (
    .PROBE_DR(io_1_probe_dr), .LED_O({io_1_led_o_5, io_1_led_o_4, io_1_led_o_3, io_1_led_o_2, io_1_led_o}),
    .KEY_I(key_1_o), .AR_I(cu_1_o[19]), .R(cu_1_o[18]), .W(cu_1_o[17]), .DR_I(cu_1_o[16]), .DR_O(cu_1_o[15]),
    .CLK(clock_1_out), .RST(RESET_out), .O(pc_1_o), .I(pc_1_o));
  Button button_3 (.out(button_3_out));
  Button V (.out(V_out));
  Button A (.out(A_out));
  Button B (.out(B_out));
  KEY key_1 (
    .CLK(clock_1_out), .RST(cu_1_o[13]), .UP(button_out), .LEFT(button_2_out), .BOTTOM(V_out),
    .RIGHT(button_3_out), .B(B_out), .A(A_out), .O(key_1_o));
  ALU alu_1 (
    .C_O(alu_1_c_o), .Z(alu_1_z), .X(AX_probe_out), .Y(pc_1_o), ._1(cu_1_o[12]),
    .OP(controlled_buffer_1_out), .C_I(ccr_1_c));
  not not_1 (not_1_out, alu_1_c_o);
  CCR ccr_1 (
    .RST(RESET_out), .CLK(clock_1_out), .I(Z_2_probe_out), .CLC(not_1_out), .SEC(alu_1_c_o), .BM(cu_1_o[14]),
    .OP(cu_1_o[10:8]), .C(ccr_1_c), .Z(ccr_1_z), .N(ccr_1_n), .BI(ccr_1_bi));
  not not_2 (not_2_out, cu_1_o[14]);
  assign controlled_buffer_1_out = not_2_out ? cu_1_o[11:8] : 4'bz;  // Controlled_Buffer controlled_buffer_1
  LED_part Z (.in(ccr_1_z));
  LED_part C (.in(ccr_1_c));
  LED_part N (.in(ccr_1_n));
  Button RESET (.out(RESET_out));
  Clock clock_1 (.out(clock_1_out));
  REGISTER AX (
    .I(pc_1_o), .R_I(cu_1_o[7]), .R_O(cu_1_o[6]), .CLK(clock_1_out), .RST(RESET_out), .O(pc_1_o),
    .PROBE_OUT(AX_probe_out));
  REGISTER BX (
    .I(pc_1_o), .R_I(cu_1_o[5]), .R_O(cu_1_o[4]), .CLK(clock_1_out), .RST(RESET_out), .O(pc_1_o),
    .PROBE_OUT(BX_probe_out));
  SP sp_1 (
    .I(pc_1_o), .R_I(cu_1_o[3]), .R_O(cu_1_o[2]), .CLK(clock_1_out), .RST(RESET_out), .O(pc_1_o),
    .PROBE_OUT(sp_1_probe_out), .ERROR(sp_1_error));
  REGISTER Z_2 (
    .I(alu_1_z), .R_I(cu_1_o[1]), .R_O(cu_1_o[0]), .CLK(clock_1_out), .RST(RESET_out), .O(pc_1_o),
    .PROBE_OUT(Z_2_probe_out));
  // Probe on pc_1_o
  // Probe on AX_probe_out
  // Probe on BX_probe_out
  // Probe on sp_1_probe_out
  LED_part OV (.in(sp_1_error));
  // Probe on Z_2_probe_out

  // Notes on the sheet:
  //   CPU
endmodule

module CU (
  input  [7:0] I,
  input  CLK,
  input  RST,
  input  OP_I,
  output [7:0] PROBE_OP,
  output [23:0] O
);

  wire comparator_1_eq, comparator_2_eq, not_1_out, not_2_out, not_3_out, or_1_out, or_2_out;
  wire [7:0] controlled_buffer_1_out, counter_1_q;
  wire [23:0] rom_1_data;

  assign controlled_buffer_1_out = OP_I ? I : 8'bz;  // Controlled_Buffer controlled_buffer_1
  not not_1 (not_1_out, CLK);
  Register OP (.D(controlled_buffer_1_out), .en(OP_I), .Q(PROBE_OP), .clk(CLK), .clr(RST));
  Counter counter_1 (
    .load(comparator_1_eq), .D(PROBE_OP), .count(not_2_out), .Q(counter_1_q), .clk(not_1_out), .clr(or_1_out));  // open: carry
  or or_1 (or_1_out, RST, comparator_2_eq);
  not not_2 (not_2_out, comparator_1_eq);
  ROM #(.dataWidth(24)) rom_1 (.addr(counter_1_q), .data(rom_1_data), .sel(1'b1));
  Comparator #(.width(24), .mode("unsigned")) comparator_1 (
    .a(rom_1_data), .b({24{1'b1}}), .eq(comparator_1_eq));  // open: gt, lt
  Comparator #(.width(24), .mode("unsigned")) comparator_2 (
    .a(rom_1_data), .b({24{1'b0}}), .eq(comparator_2_eq));  // open: gt, lt
  Pull_Resistor pull_resistor_1 (.node(O));
  assign O = not_3_out ? rom_1_data : 24'bz;  // Controlled_Buffer controlled_buffer_2
  not not_3 (not_3_out, or_2_out);
  or or_2 (or_2_out, comparator_1_eq, comparator_2_eq);

  // Notes on the sheet:
  //   CONTROL UNIT
  //   JUMP TO OP
  //   RESET COUNTER
  //   contents of rom_1 (hex, n*v repeats v):
  //   280000 50000 908000 280000 150000 ffffff 8080 0 88000 50000 8080 0 88000 50000 88000 50000 8080 0
  //   8020 0 88000 50000 8020 0 88000 50000 88000 50000 8020 0 88000 50000 8102 80001 50000 8020 0 8102
  //   80001 50000 88000 50000 8020 0 88000 10040 28000 0 88000 50000 88000 50000 8080 0 8102 80001 10010
  //   28000 0 88000 10010 28000 0 88000 50000 88000 10010 28000 0 88000 50000 8102 80001 10010 28000 0
  //   8102 80001 50000 88000 10010 28000 0 60 0 90 0 8102 81 0 88000 50000 8102 81 0 8202 81 0 88000 50000
  //   8202 81 0 1102 81 0 1202 81 0 8302 81 0 88000 50000 8302 81 0 8402 81 0 88000 50000 8402 81 0 8502
  //   81 0 88000 50000 8502 81 0 602 81 0 702 81 0 802 81 0 902 81 0 a02 81 0 4000 0 4100 0 4200 0 4300 0
  //   4400 0 4500 0 4600 0 4700 0 8202 0 88000 50000 8202 0 80004 10040 28000 84 1102 9 8080 0 84 1202
  //   80009 50000 8080 0 400000 0 88000 50000 400000 0 8080 80004 210000 28000 10040 400000 84 1102 9 0
  //   88000 50000 200080 400000 10040 80084 1102 9 0 84 1202 80009 50000 400000 0 2000 0 8102 80001 50000
  //   8020
endmodule

module RAM (
  input  AR_I,
  input  R,
  input  W,
  input  DR_I,
  input  DR_O,
  input  CLK,
  input  RST,
  input  [7:0] I,
  output [7:0] PROBE_DR,
  output [7:0] O
);

  wire or_1_out, or_2_out, or_3_out;
  wire [7:0] AR_2_o, AR_2_probe_out, controlled_buffer_2_out, DR_o_2, ram_1_data;

  // Probe on AR_2_probe_out
  REGISTER AR_2 (.I(I), .R_I(AR_I), .R_O(1'b1), .CLK(CLK), .RST(RST), .O(AR_2_o), .PROBE_OUT(AR_2_probe_out));
  or or_1 (or_1_out, W, R);
  RAM_part ram_1 (.addr(AR_2_o), .data(ram_1_data), .sel(or_1_out), .clk(CLK), .ld(R));  // open: clr
  assign ram_1_data = W ? DR_o_2 : 8'bz;  // Controlled_Buffer controlled_buffer_1
  assign controlled_buffer_2_out = R ? ram_1_data : 8'bz;  // Controlled_Buffer controlled_buffer_2
  or or_2 (or_2_out, DR_O, R);
  or or_3 (or_3_out, DR_I, AR_I, W);
  REGISTER DR (
    .I(controlled_buffer_2_out), .R_I(DR_I), .R_O(DR_O), .CLK(CLK), .RST(RST), .O(DR_o_2),
    .PROBE_OUT(PROBE_DR));
  // Probe on PROBE_DR
  assign controlled_buffer_2_out = or_3_out ? I : 8'bz;  // Controlled_Buffer controlled_buffer_3
  assign O = or_2_out ? DR_o_2 : 8'bz;  // Controlled_Buffer controlled_buffer_4

  // Notes on the sheet:
  //   RANDOM ACCESS MEMORY
  //   RAM
endmodule

module REGISTER (
  input  [7:0] I,
  input  R_I,
  input  R_O,
  input  CLK,
  input  RST,
  output [7:0] O,
  output [7:0] PROBE_OUT
);

  wire [7:0] controlled_buffer_1_out;

  assign controlled_buffer_1_out = R_I ? I : 8'bz;  // Controlled_Buffer controlled_buffer_1
  Register R (.D(controlled_buffer_1_out), .Q(PROBE_OUT), .clk(CLK), .clr(RST));  // open: en
  assign O = R_O ? PROBE_OUT : 8'bz;  // Controlled_Buffer controlled_buffer_2

  // Notes on the sheet:
  //   8BIT REGISTER
endmodule

module ALU (
  input  [7:0] X,
  input  [7:0] Y,
  input  _1,
  input  [3:0] OP,
  input  C_I,
  output C_O,
  output [7:0] Z
);

  wire and_2_out, comparator_1_lt, fulladder_8bit_1_c_o, not_1_out, pull_resistor_3_node;
  wire [3:0] subtractor_1_out;
  wire [7:0] and_1_out, controlled_buffer_1_out, fulladder_8bit_1_z, or_1_out, shifter_1_out, shifter_2_out,
       shifter_3_out, shifter_4_out, shifter_5_out, xor_1_out;

  not not_1 (not_1_out, _1);
  Pull_Resistor pull_resistor_1 (.node(C_I));
  assign controlled_buffer_1_out = _1 ? 8'h1 : 8'bz;  // Controlled_Buffer controlled_buffer_1
  Pull_Resistor pull_resistor_2 (.node(Y));
  assign controlled_buffer_1_out = not_1_out ? Y : 8'bz;  // Controlled_Buffer controlled_buffer_2
  assign C_I = comparator_1_lt ? pull_resistor_3_node : 1'bz;  // Controlled_Buffer controlled_buffer_3
  Pull_Resistor pull_resistor_3 (.node(pull_resistor_3_node));
  FULLADDER_8BIT fulladder_8bit_1 (
    .X(X), .Y(controlled_buffer_1_out), .SUB(and_2_out), .C_I(pull_resistor_3_node), .Z(fulladder_8bit_1_z),
    .C_O(fulladder_8bit_1_c_o));
  assign and_1_out = X & controlled_buffer_1_out;  // AND_Gate and_1, 8 bits wide
  assign or_1_out = X | controlled_buffer_1_out;  // OR_Gate or_1, 8 bits wide
  assign xor_1_out = X ^ X;  // XOR_Gate xor_1, 8 bits wide
  Shifter shifter_1 (.in(X), .\dist (3'b001), .out(shifter_1_out));
  Shifter #(.shift("lr")) shifter_2 (.in(X), .\dist (3'b001), .out(shifter_2_out));
  Shifter #(.shift("ar")) shifter_3 (.in(X), .\dist (3'b001), .out(shifter_3_out));
  Shifter #(.shift("rl")) shifter_4 (.in(X), .\dist (3'b001), .out(shifter_4_out));
  Shifter #(.shift("rr")) shifter_5 (.in(X), .\dist (3'b001), .out(shifter_5_out));
  and and_2 (and_2_out, subtractor_1_out[0], ~subtractor_1_out[1], ~subtractor_1_out[2], ~subtractor_1_out[3]);  // AND_Gate
  assign C_O = comparator_1_lt ? fulladder_8bit_1_c_o : 1'bz;  // Controlled_Buffer controlled_buffer_4
  Comparator #(.width(4)) comparator_1 (.a(subtractor_1_out), .b(4'b0100), .lt(comparator_1_lt));  // open: gt, eq
  Pull_Resistor pull_resistor_4 (.node(C_O));
  Multiplexer #(.select(4), .width(8), .disabled(0), .enable("false")) multiplexer_1 (
    .in0(fulladder_8bit_1_z), .in1(fulladder_8bit_1_z), .in2(and_1_out), .in3(or_1_out), .in4(xor_1_out),
    .in5(shifter_1_out), .in6(shifter_2_out), .in7(shifter_3_out), .in8(shifter_4_out), .in9(shifter_5_out),
    .out(Z), .sel(subtractor_1_out));  // open: in10, in11, in12, in13, in14, in15
  Subtractor #(.width(4)) subtractor_1 (.a(OP), .b(4'b0001), .out(subtractor_1_out));  // open: bin, bout

  // Notes on the sheet:
  //   ALU
endmodule

// +/-
module FULLADDER_8BIT (
  input  [7:0] X,
  input  [7:0] Y,
  input  SUB,
  input  C_I,
  output [7:0] Z,
  output C_O
);

  wire fulladder_1bit_1_c_o, fulladder_1bit_2_c_o, fulladder_1bit_3_c_o, fulladder_1bit_4_c_o,
       fulladder_1bit_5_c_o, fulladder_1bit_6_c_o, fulladder_1bit_7_c_o, or_1_out, xor_1_out, xor_2_out,
       xor_3_out, xor_4_out, xor_5_out, xor_6_out, xor_7_out, xor_8_out;

  or or_1 (or_1_out, SUB, C_I);
  xor xor_1 (xor_1_out, SUB, Y[0]);
  xor xor_2 (xor_2_out, SUB, Y[1]);
  xor xor_3 (xor_3_out, SUB, Y[2]);
  xor xor_4 (xor_4_out, SUB, Y[3]);
  xor xor_5 (xor_5_out, SUB, Y[4]);
  xor xor_6 (xor_6_out, SUB, Y[5]);
  xor xor_7 (xor_7_out, SUB, Y[6]);
  xor xor_8 (xor_8_out, SUB, Y[7]);
  FULLADDER_1BIT fulladder_1bit_1 (.X(X[0]), .Y(xor_1_out), .C_I(or_1_out), .C_O(fulladder_1bit_1_c_o), .Z(Z[0]));
  FULLADDER_1BIT fulladder_1bit_2 (
    .X(X[1]), .Y(xor_2_out), .C_I(fulladder_1bit_1_c_o), .C_O(fulladder_1bit_2_c_o), .Z(Z[1]));
  FULLADDER_1BIT fulladder_1bit_3 (
    .X(X[2]), .Y(xor_3_out), .C_I(fulladder_1bit_2_c_o), .C_O(fulladder_1bit_3_c_o), .Z(Z[2]));
  FULLADDER_1BIT fulladder_1bit_4 (
    .X(X[3]), .Y(xor_4_out), .C_I(fulladder_1bit_3_c_o), .C_O(fulladder_1bit_4_c_o), .Z(Z[3]));
  FULLADDER_1BIT fulladder_1bit_5 (
    .X(X[4]), .Y(xor_5_out), .C_I(fulladder_1bit_4_c_o), .C_O(fulladder_1bit_5_c_o), .Z(Z[4]));
  FULLADDER_1BIT fulladder_1bit_6 (
    .X(X[5]), .Y(xor_6_out), .C_I(fulladder_1bit_5_c_o), .C_O(fulladder_1bit_6_c_o), .Z(Z[5]));
  FULLADDER_1BIT fulladder_1bit_7 (
    .X(X[6]), .Y(xor_7_out), .C_I(fulladder_1bit_6_c_o), .C_O(fulladder_1bit_7_c_o), .Z(Z[6]));
  FULLADDER_1BIT fulladder_1bit_8 (.X(X[7]), .Y(xor_8_out), .C_I(fulladder_1bit_7_c_o), .C_O(C_O), .Z(Z[7]));

  // Notes on the sheet:
  //   FULL ADDER 8BIT
endmodule

module FULLADDER_1BIT (
  input  X,
  input  Y,
  input  C_I,
  output C_O,
  output Z
);

  wire and_1_out, and_2_out, xor_1_out;

  and and_1 (and_1_out, X, Y);
  xor xor_1 (xor_1_out, X, Y);
  or or_1 (C_O, and_1_out, and_2_out);
  and and_2 (and_2_out, xor_1_out, C_I);
  xor xor_2 (Z, xor_1_out, C_I);

  // Notes on the sheet:
  //   FULL ADDER 1BIT
endmodule

module CCR (
  input  RST,
  input  CLK,
  input  [7:0] I,
  input  CLC,
  input  SEC,
  input  BM,
  input  [2:0] OP,
  output C,
  output Z,
  output N,
  output BI
);

  wire and_1_out, and_2_out, BCC_out, BCS_out, BEQ_out, BMI_out, BNE_out, BPL_out, demultiplexer_1_out0,
       demultiplexer_1_out1, demultiplexer_1_out2, demultiplexer_1_out3, demultiplexer_1_out4,
       demultiplexer_1_out5, demultiplexer_1_out6, demultiplexer_1_out7, or_1_out, or_2_out, or_3_out;

  or or_1 (or_1_out, CLC, demultiplexer_1_out7);
  or or_2 (or_2_out, SEC, demultiplexer_1_out6);
  J_K_Flip_Flop u_C (.J(or_2_out), .clk(CLK), .K(or_1_out), .Q(C), .en(or_3_out), .reset(RST));  // open: Qn, preset
  or or_3 (or_3_out, and_2_out, and_1_out);
  and and_1 (and_1_out, ~BM, ~OP[2], OP[1], ~OP[0]);  // AND_Gate
  and and_2 (and_2_out, ~BM, ~OP[2], ~OP[1], OP[0]);  // AND_Gate
  Comparator comparator_1 (.a(I), .b({8{1'b0}}), .eq(Z));  // open: gt, lt
  BitSelector bitselector_1 (.in(I), .out(N), .sel(3'b111));
  Demultiplexer #(.select(3), .disabled(0)) demultiplexer_1 (
    .out0(demultiplexer_1_out0), .out1(demultiplexer_1_out1), .out2(demultiplexer_1_out2),
    .out3(demultiplexer_1_out3), .out4(demultiplexer_1_out4), .out5(demultiplexer_1_out5),
    .out6(demultiplexer_1_out6), .out7(demultiplexer_1_out7), .in(1'b1), .sel(OP), .en(BM));
  and BPL (BPL_out, ~N, demultiplexer_1_out0);  // AND_Gate
  and BMI (BMI_out, N, demultiplexer_1_out1);
  and BCC (BCC_out, ~C, demultiplexer_1_out2);  // AND_Gate
  and BCS (BCS_out, C, demultiplexer_1_out3);
  and BNE (BNE_out, ~Z, demultiplexer_1_out4);  // AND_Gate
  and BEQ (BEQ_out, Z, demultiplexer_1_out5);
  or or_4 (BI, BPL_out, BMI_out, BCC_out, BCS_out, BNE_out, BEQ_out);

  // Notes on the sheet:
  //   CONDITION CODE REGISTER
  //   CLC
  //   SEC
endmodule

module PC (
  input  PC_I,
  input  [7:0] I,
  input  PC_O,
  input  CLK,
  input  RST,
  input  plus_1,
  output [7:0] O
);

  wire [7:0] adder_1_out, controlled_buffer_1_out, controlled_buffer_3_out, register_1_q;

  assign controlled_buffer_1_out = PC_I ? I : 8'bz;  // Controlled_Buffer controlled_buffer_1
  Register register_1 (.D(controlled_buffer_1_out), .Q(register_1_q), .clk(CLK), .clr(RST));  // open: en
  assign O = PC_O ? register_1_q : 8'bz;  // Controlled_Buffer controlled_buffer_2
  assign controlled_buffer_3_out = plus_1 ? register_1_q : 8'bz;  // Controlled_Buffer controlled_buffer_3
  assign controlled_buffer_1_out = plus_1 ? adder_1_out : 8'bz;  // Controlled_Buffer controlled_buffer_4
  Adder adder_1 (.a(controlled_buffer_3_out), .b(8'h1), .out(adder_1_out));  // open: cin, cout

  // Notes on the sheet:
  //   PROGRAM COUNTER
endmodule

module SP (
  input  [7:0] I,
  input  R_I,
  input  R_O,
  input  CLK,
  input  RST,
  output [7:0] O,
  output [7:0] PROBE_OUT,
  output ERROR
);

  wire comparator_1_lt, comparator_2_gt, or_1_out;
  wire [7:0] controlled_buffer_1_out;

  assign controlled_buffer_1_out = R_I ? I : 8'bz;  // Controlled_Buffer controlled_buffer_1
  assign controlled_buffer_1_out = RST ? 8'he0 : 8'bz;  // Controlled_Buffer controlled_buffer_2
  Register R (.D(controlled_buffer_1_out), .Q(PROBE_OUT), .clk(or_1_out));  // open: en, clr
  or or_1 (or_1_out, CLK, RST);
  assign O = R_O ? PROBE_OUT : 8'bz;  // Controlled_Buffer controlled_buffer_3
  Comparator #(.mode("unsigned")) comparator_1 (.a(PROBE_OUT), .b(8'he0), .lt(comparator_1_lt));  // open: gt, eq
  or or_2 (ERROR, comparator_1_lt, comparator_2_gt);
  Comparator #(.mode("unsigned")) comparator_2 (.a(PROBE_OUT), .b(8'he4), .gt(comparator_2_gt));  // open: eq, lt

  // Notes on the sheet:
  //   STACK POINTER
  //   STACK BEGIN
  //   STACK END
endmodule

// I/O
module IO (
  input  AR_I,
  input  R,
  input  W,
  input  DR_I,
  input  DR_O,
  input  [2:0] KEY_I,
  input  CLK,
  input  RST,
  input  [7:0] I,
  output [7:0] PROBE_DR,
  output [24:0] LED_O,
  output [7:0] O
);

  wire and_1_out, and_2_out, and_3_out, and_4_out, and_5_out, comparator_1_gt, comparator_1_lt,
       comparator_2_gt, comparator_2_lt, comparator_3_eq, comparator_4_eq, or_1_out, or_2_out, or_3_out,
       or_4_out;
  wire [4:0] subtractor_1_out;
  wire [7:0] AR_o, AR_probe_out, controlled_buffer_1_out, controlled_buffer_4_out, DR_2_o, RND_out;

  REGISTER AR (.I(I), .R_I(AR_I), .R_O(1'b1), .CLK(CLK), .RST(RST), .O(AR_o), .PROBE_OUT(AR_probe_out));
  // Probe on AR_probe_out
  Comparator #(.mode("unsigned")) comparator_1 (
    .a(AR_o), .b(8'he5), .gt(comparator_1_gt), .lt(comparator_1_lt));  // open: eq
  Comparator #(.mode("unsigned")) comparator_2 (
    .a(AR_o), .b(8'hfd), .gt(comparator_2_gt), .lt(comparator_2_lt));  // open: eq
  Comparator #(.mode("unsigned")) comparator_3 (.a(AR_o), .b({8{1'b1}}), .eq(comparator_3_eq));  // open: gt, lt
  Comparator #(.mode("unsigned")) comparator_4 (.a(AR_o), .b(8'hfe), .eq(comparator_4_eq));  // open: gt, lt
  Random RND (.clk(CLK), .next(1'b1), .out(RND_out));  // open: clr
  assign controlled_buffer_1_out = comparator_3_eq ? RND_out : 8'bz;  // Controlled_Buffer controlled_buffer_1
  LED_part RAM (.in(and_1_out));
  and and_1 (and_1_out, ~comparator_1_gt, comparator_1_lt);  // AND_Gate
  and and_2 (and_2_out, comparator_2_gt, ~comparator_2_lt);  // AND_Gate
  assign controlled_buffer_1_out = comparator_4_eq ? {{5{1'b0}}, KEY_I} : 8'bz;  // Controlled_Buffer controlled_buffer_2
  LED_part LED (.in(and_3_out));
  LED_part IO (.in(and_2_out));
  and and_3 (and_3_out, ~and_1_out, ~and_2_out);  // AND_Gate
  Subtractor #(.width(5)) subtractor_1 (.a(AR_o[4:0]), .b(5'b00101), .out(subtractor_1_out));  // open: bin, bout
  // Probe on KEY_I
  and and_4 (and_4_out, and_1_out, or_1_out);
  or or_1 (or_1_out, W, R);
  LED led_2 (
    .RST(RST), .CLK(CLK), .A(subtractor_1_out), .ENABLE(and_5_out), .R(R), .W(W),
    .I(controlled_buffer_1_out), .O(controlled_buffer_1_out), .LED_OUT(LED_O));
  and and_5 (and_5_out, and_3_out, or_2_out);
  or or_2 (or_2_out, W, R);
  RAM_part ram_2 (.addr(AR_o), .data(controlled_buffer_1_out), .sel(and_4_out), .clk(CLK), .ld(R));  // open: clr
  assign controlled_buffer_1_out = W ? DR_2_o : 8'bz;  // Controlled_Buffer controlled_buffer_3
  assign controlled_buffer_4_out = R ? controlled_buffer_1_out : 8'bz;  // Controlled_Buffer controlled_buffer_4
  // Probe on PROBE_DR
  or or_3 (or_3_out, DR_O, R);
  or or_4 (or_4_out, DR_I, AR_I, W);
  REGISTER DR_2 (
    .I(controlled_buffer_4_out), .R_I(DR_I), .R_O(DR_O), .CLK(CLK), .RST(RST), .O(DR_2_o),
    .PROBE_OUT(PROBE_DR));
  assign controlled_buffer_4_out = or_4_out ? I : 8'bz;  // Controlled_Buffer controlled_buffer_5
  assign O = or_3_out ? DR_2_o : 8'bz;  // Controlled_Buffer controlled_buffer_6

  // Notes on the sheet:
  //   I/O CONTROLLER
  //   RAM
  //   LED
endmodule

module LED (
  input  RST,
  input  CLK,
  input  [4:0] A,
  input  ENABLE,
  input  R,
  input  W,
  input  [7:0] I,
  output [24:0] LED_OUT,
  output [7:0] O
);

  wire and_1_out, and_2_out, comparator_1_gt, not_1_out, or_1_out;
  wire [4:0] adder_1_out, counter_1_q, multiplexer_1_out;
  wire [7:0] controlled_buffer_1_out, controlled_buffer_2_out;
  wire [24:0] and_3_out, multiplexer_2_out, not_2_out, or_2_out, shifter_1_out;

  Counter #(.width(5), .max('h18)) counter_1 (.Q(counter_1_q), .clk(CLK), .clr(RST));  // open: load, D, count, carry
  Multiplexer #(.width(5), .disabled(0), .enable("false")) multiplexer_1 (
    .in0(counter_1_q), .in1(A), .out(multiplexer_1_out), .sel(ENABLE));
  not not_1 (not_1_out, ENABLE);
  or or_1 (or_1_out, R, not_1_out);
  assign controlled_buffer_1_out = and_1_out ? I : 8'bz;  // Controlled_Buffer controlled_buffer_1
  and and_1 (and_1_out, ENABLE, W);
  Adder #(.width(5)) adder_1 (.a(5'b00001), .b(counter_1_q), .out(adder_1_out));  // open: cin, cout
  // Probe on shifter_1_out
  Shifter #(.width(25), .shift("rr")) shifter_1 (.in(25'h1), .\dist (adder_1_out), .out(shifter_1_out));
  assign controlled_buffer_2_out = not_1_out ? controlled_buffer_1_out : 8'bz;  // Controlled_Buffer controlled_buffer_2
  RAM_part #(.addrWidth(5)) ram_1 (
    .addr(multiplexer_1_out), .data(controlled_buffer_1_out), .sel(1'b1), .clk(CLK), .ld(or_1_out), .clr(RST));
  and and_2 (and_2_out, ENABLE, ~W);  // AND_Gate
  assign O = and_2_out ? controlled_buffer_1_out : 8'bz;  // Controlled_Buffer controlled_buffer_3
  // Probe on not_2_out
  assign not_2_out = ~shifter_1_out;  // NOT_Gate not_2, 25 bits wide
  Comparator #(.mode("unsigned")) comparator_1 (
    .a(controlled_buffer_2_out), .b({8{1'b0}}), .gt(comparator_1_gt));  // open: eq, lt
  assign and_3_out = not_2_out & LED_OUT;  // AND_Gate and_3, 25 bits wide
  assign or_2_out = shifter_1_out | LED_OUT;  // OR_Gate or_2, 25 bits wide
  Multiplexer #(.width(25), .disabled(0), .enable("false")) multiplexer_2 (
    .in0(and_3_out), .in1(or_2_out), .out(multiplexer_2_out), .sel(comparator_1_gt));
  Register #(.width(25)) register_1 (.D(multiplexer_2_out), .en(not_1_out), .Q(LED_OUT), .clk(CLK), .clr(RST));

  // Notes on the sheet:
  //   LED CONTROLLER
endmodule

module KEY (
  input  UP,
  input  LEFT,
  input  BOTTOM,
  input  RIGHT,
  input  B,
  input  A,
  input  CLK,
  input  RST,
  output [2:0] O
);

  wire and_1_out, and_2_out, and_3_out, and_4_out, controlled_buffer_1_out, j_k_ff_1_q, j_k_ff_2_q,
       j_k_ff_2_qn, or_1_out;
  wire [2:0] controlled_buffer_2_out, controlled_buffer_3_out;

  J_K_Flip_Flop j_k_ff_1 (.Q(j_k_ff_1_q), .preset(RST), .reset(controlled_buffer_1_out));  // open: J, clk, K, Qn, en
  and and_1 (and_1_out, ~or_1_out, j_k_ff_1_q);  // AND_Gate
  LED_part KEY_PRESSED (.in(or_1_out));
  LED_part DISABLED (.in(j_k_ff_2_q));
  J_K_Flip_Flop j_k_ff_2 (
    .J(1'b0), .clk(CLK), .K(and_1_out), .Q(j_k_ff_2_q), .Qn(j_k_ff_2_qn), .preset(controlled_buffer_1_out));  // open: en, reset
  assign controlled_buffer_1_out = j_k_ff_2_qn ? or_1_out : 1'bz;  // Controlled_Buffer controlled_buffer_1
  and and_2 (and_2_out, controlled_buffer_1_out, ~controlled_buffer_2_out[2]);  // AND_Gate
  J_K_Flip_Flop j_k_ff_3 (
    .J(1'b0), .clk(CLK), .K(RST), .Q(O[2]), .preset(controlled_buffer_2_out[2]), .en(RST), .reset(and_2_out));  // open: Qn
  or or_1 (or_1_out, UP, LEFT, BOTTOM, RIGHT, B, A);
  assign controlled_buffer_2_out = j_k_ff_2_qn ? controlled_buffer_3_out : 3'bz;  // Controlled_Buffer controlled_buffer_2
  and and_3 (and_3_out, controlled_buffer_1_out, ~controlled_buffer_2_out[1]);  // AND_Gate
  J_K_Flip_Flop j_k_ff_4 (
    .J(1'b0), .clk(CLK), .K(RST), .Q(O[1]), .preset(controlled_buffer_2_out[1]), .en(RST), .reset(and_3_out));  // open: Qn
  assign controlled_buffer_3_out = UP ? 3'b001 : 3'bz;  // Controlled_Buffer controlled_buffer_3
  and and_4 (and_4_out, controlled_buffer_1_out, ~controlled_buffer_2_out[0]);  // AND_Gate
  J_K_Flip_Flop j_k_ff_5 (
    .J(1'b0), .clk(CLK), .K(RST), .Q(O[0]), .preset(controlled_buffer_2_out[0]), .en(RST), .reset(and_4_out));  // open: Qn
  assign controlled_buffer_3_out = BOTTOM ? 3'b011 : 3'bz;  // Controlled_Buffer controlled_buffer_4
  assign controlled_buffer_3_out = LEFT ? 3'b010 : 3'bz;  // Controlled_Buffer controlled_buffer_5
  assign controlled_buffer_3_out = RIGHT ? 3'b100 : 3'bz;  // Controlled_Buffer controlled_buffer_6
  assign controlled_buffer_3_out = A ? 3'b110 : 3'bz;  // Controlled_Buffer controlled_buffer_7
  assign controlled_buffer_3_out = B ? 3'b101 : 3'bz;  // Controlled_Buffer controlled_buffer_8
  Pull_Resistor pull_resistor_1 (.node(controlled_buffer_3_out));

  // Notes on the sheet:
  //   RIGHT: pull=up
  //   B: pull=up
  //   RST: pull=down
  //   A: pull=up
  //   UP: pull=up
  //   BOTTOM: pull=up
  //   CLK: pull=down
  //   LEFT: pull=up
  //   KEYBOARD CONTROLLER
endmodule
